# Fritzing sketch sketch (saved by Fritzing 0.9.3b)
breadboards: 1

parts:
  Part1 = Arduino Uno (Rev3)
  R1 = Resistor [tolerance=±5% resistance=10k package=THT]
  R2 = Resistor [tolerance=±5% resistance=10k package=THT]
  S1 = Pushbutton [package="[THT]"]
  S2 = Pushbutton [package="[THT]"]
  R3 = Resistor [tolerance=±5% resistance=1k package=THT]
  R4 = Resistor [tolerance=±5% resistance=470 package=THT]
  JP1 = RCA [package=rca_lock]

nets:
  N1: Part1.D9_PWM, R3.Pin_1
  N2: Part1.GND, R1.Pin_1, S1.Pin_3, S1.Pin_4, S2.Pin_3, S2.Pin_4, JP1.PIN
  N3: Part1.D2, R2.Pin_0, S2.Pin_1, S2.Pin_2
  N4: Part1.D3_PWM, R1.Pin_0, S1.Pin_1, S1.Pin_2
  N5: Part1.D7, R4.Pin_1
  N6: R3.Pin_0, R4.Pin_0, JP1.SHELL
